// Logisim project ttt_wkt.circ as structural Verilog: 1 circuit, main circuit main
module main (
);

  wire b1, b2, b3, b4, b5, b6, b7, b8, b9, button_8_out, clock_1_out, clock_2_out, clock_3_out, p1, p2, p3,
       p4, p5, p6, p7, p8, p9, Reset, Tie, WhoFirst, Win;
  wire [3:0] register_1_q, rom_1_data, Xstate;
  wire [8:0] demultiplexer_1_out1, Omoves;

  Clock clock_1 (.out(clock_1_out));
  Clock clock_2 (.out(clock_2_out));
  // Probe on Omoves
  Register #(.width(4)) register_1 (.D(Xstate), .Q(register_1_q), .clk(clock_1_out), .clr(Reset));  // open: en
  J_K_Flip_Flop j_k_ff_1 (.J(p1), .clk(clock_2_out), .K(b1), .Q(Omoves[0]), .reset(Reset));  // open: Qn, preset, en
  J_K_Flip_Flop j_k_ff_2 (.J(p2), .clk(clock_2_out), .K(b2), .Q(Omoves[1]), .reset(Reset));  // open: Qn, preset, en
  J_K_Flip_Flop j_k_ff_3 (.J(p3), .clk(clock_2_out), .K(b3), .Q(Omoves[2]), .reset(Reset));  // open: Qn, preset, en
  J_K_Flip_Flop j_k_ff_4 (.J(p4), .clk(clock_2_out), .K(b4), .Q(Omoves[3]), .reset(Reset));  // open: Qn, preset, en
  J_K_Flip_Flop j_k_ff_5 (.J(p5), .clk(clock_2_out), .K(b5), .Q(Omoves[4]), .reset(Reset));  // open: Qn, preset, en
  J_K_Flip_Flop j_k_ff_6 (.J(p6), .clk(clock_2_out), .K(b6), .Q(Omoves[5]), .reset(Reset));  // open: Qn, preset, en
  J_K_Flip_Flop j_k_ff_7 (.J(p7), .clk(clock_2_out), .K(b7), .Q(Omoves[6]), .reset(Reset));  // open: Qn, preset, en
  J_K_Flip_Flop j_k_ff_8 (.J(p8), .clk(clock_2_out), .K(b8), .Q(Omoves[7]), .reset(Reset));  // open: Qn, preset, en
  J_K_Flip_Flop j_k_ff_9 (.J(p9), .clk(clock_2_out), .K(b9), .Q(Omoves[8]), .reset(Reset));  // open: Qn, preset, en
  // Probe on {WhoFirst, register_1_q, Omoves}
  // Probe on {Xstate, rom_1_data}
  ROM #(.addrWidth(14)) rom_1 (.addr({WhoFirst, register_1_q, Omoves}), .data({Xstate, rom_1_data}));  // open: sel
  Clock clock_3 (.out(clock_3_out));
  J_K_Flip_Flop j_k_ff_10 (
    .J(demultiplexer_1_out1[0]), .clk(clock_3_out), .K(1'b0), .Q(b1), .reset(Reset));  // open: Qn, preset, en
  J_K_Flip_Flop j_k_ff_11 (
    .J(demultiplexer_1_out1[1]), .clk(clock_3_out), .K(1'b0), .Q(b2), .reset(Reset));  // open: Qn, preset, en
  J_K_Flip_Flop j_k_ff_12 (
    .J(demultiplexer_1_out1[2]), .clk(clock_3_out), .K(1'b0), .Q(b3), .reset(Reset));  // open: Qn, preset, en
  J_K_Flip_Flop j_k_ff_13 (
    .J(demultiplexer_1_out1[3]), .clk(clock_3_out), .K(1'b0), .Q(b4), .reset(Reset));  // open: Qn, preset, en
  J_K_Flip_Flop j_k_ff_14 (
    .J(demultiplexer_1_out1[4]), .clk(clock_3_out), .K(1'b0), .Q(b5), .reset(Reset));  // open: Qn, preset, en
  J_K_Flip_Flop j_k_ff_15 (
    .J(demultiplexer_1_out1[5]), .clk(clock_3_out), .K(1'b0), .Q(b6), .reset(Reset));  // open: Qn, preset, en
  J_K_Flip_Flop j_k_ff_16 (
    .J(demultiplexer_1_out1[6]), .clk(clock_3_out), .K(1'b0), .Q(b7), .reset(Reset));  // open: Qn, preset, en
  J_K_Flip_Flop j_k_ff_17 (
    .J(demultiplexer_1_out1[7]), .clk(clock_3_out), .K(1'b0), .Q(b8), .reset(Reset));  // open: Qn, preset, en
  J_K_Flip_Flop j_k_ff_18 (
    .J(demultiplexer_1_out1[8]), .clk(clock_3_out), .K(1'b0), .Q(b9), .reset(Reset));  // open: Qn, preset, en
  Demultiplexer #(.select(4), .enable("false")) demultiplexer_1 (
    .out1(demultiplexer_1_out1[0]), .out2(demultiplexer_1_out1[1]), .out3(demultiplexer_1_out1[2]),
    .out4(demultiplexer_1_out1[3]), .out5(demultiplexer_1_out1[4]), .out6(demultiplexer_1_out1[5]),
    .out7(demultiplexer_1_out1[6]), .out8(demultiplexer_1_out1[7]), .out9(demultiplexer_1_out1[8]),
    .out14(Tie), .out15(Win), .in(1'b1), .sel(rom_1_data));  // open: out0, out10, out11, out12, out13
  LED led_1 (.in(Omoves[0]));
  Button button_1 (.out(p1));
  LED led_2 (.in(Omoves[3]));
  Button button_2 (.out(p4));
  LED led_3 (.in(Omoves[6]));
  Button button_3 (.out(p7));
  Button button_4 (.out(Reset));
  LED led_4 (.in(b1));
  Button button_5 (.out(p2));
  LED led_5 (.in(b4));
  Button button_6 (.out(p5));
  LED led_6 (.in(b7));
  Button button_7 (.out(p8));
  Button button_8 (.out(button_8_out));
  LED led_7 (.in(Omoves[1]));
  Button button_9 (.out(p3));
  LED led_8 (.in(b2));
  LED led_9 (.in(b5));
  Button button_10 (.out(p6));
  LED led_10 (.in(Omoves[4]));
  LED led_11 (.in(Omoves[7]));
  LED led_12 (.in(b8));
  Button button_11 (.out(p9));
  LED led_13 (.in(Tie));
  T_Flip_Flop t_ff_1 (.clk(button_8_out), .T(1'b1), .Q(WhoFirst));  // open: Qn, preset, reset, en
  LED led_14 (.in(b3));
  LED led_15 (.in(Omoves[2]));
  LED led_16 (.in(b6));
  LED led_17 (.in(Omoves[5]));
  LED led_18 (.in(Omoves[8]));
  LED led_19 (.in(b9));
  LED led_20 (.in(Win));

  // Other names for the same wires on the sheet: u1 = Omoves[0]; u2 = Omoves[1]; u3 = Omoves[2]; u4 = Omoves[3];
  //   u5 = Omoves[4]; u6 = Omoves[5]; u7 = Omoves[6]; u8 = Omoves[7]; u9 = Omoves[8];
  //   Xmoves[8:0] = {b9, b8, b7, b6, b5, b4, b3, b2, b1}

  // Notes on the sheet:
  //   contents of rom_1 (hex, n*v repeats v):
  //   0 55 81 0 55 0 0 0 81 0 0 f 0 f 0 0 81 5*0 f 0 6 0 18 0 27 0 f 0 13 0 0 f 0 f f 0 0 f 0 0 0 f f 0 0
  //   9 f 18 f 11*0 55 5*0 4 17*0 23 0 f 6*0 f 0 8 f f 29 0 0 0 f 0 f 4*0 12 1 13*0 22 5*0 1 0 0 f 0 0 0 6
  //   6*0 f 0 0 0 52 6 0 0 0 e 4*0 f f 0 2 17 10*0 12 17*0 f 0 4 26 0 1 0 f 0 35 4*0 f 6*0 93 7*0 1 2 f 0
  //   35 e 0 0 93 7*0 93 15*0 55 12*0 f 6*0 f 0 f 0 52 9*0 f f 14*0 1 14*0 f 0 f f 0 26 0 f 0 0 0 f 5*0 4
  //   13*0 f 8 8 e 4*0 f 9*0 e 14*0 f 0 f 0 5 26 0 f 0 0 0 6 e 10*0 f 7*0 f f f 5*0 f 7*0 f 88*0 17 0 3 0
  //   52 12*0 16 0 0 0 37 0 13 74 74 0 19 42 31 0 35 52 11 0 31 1f 0 0 74 0 0 18 38*0 33 5*0 91 0 15 0 31
  //   1f 0 0 11 0 9 5*0 11 12 8 1e 21*0 3 13 17*0 11 0 0 0 91 0 13 0 31 19 1f 0 11 0 37 0 15 1e 0 0 0 12
  //   14*0 19 74 31 0 31 1f 0 0 31 0 9 6*0 13 14*0 31 13 9 5*0 82 7*0 62 1e 23*0 52 13 0 0 1f 12*0 33 0 12
  //   0 0 0 91 0 13 5*0 11 0 37 5*0 11 0 77 13*0 18 2 31 0 2 1f 16 0 2 0 48 0 18 0 1e 17*0 2 1f 48 5*0 82
  //   7*0 62 15*0 17 3 d1 0 46 1f 1f 0 3 0 37 0 11 7*0 11 0 0 0 11 0 0 0 1e 0 0 0 3 0 37 5*0 82 7*0 62
  //   97*0 28 0 0 0 57 0 0 0 16 0 26 0 38 19*0 34 16*0 2f 14*0 63 5*0 23 0 9 11*0 2f 25*0 22 67 0 0 67 2f
  //   0 0 67 7*0 b1 29 0 0 0 64 0 0 0 6 0 0 12 0 0 0 67 0 0 0 29 64 2f 5*0 15 4*0 64 0 0 64 11*0 69 2f 0
  //   4*2f 17*0 32 8*0 29 29 2e 2f 32*0 22 2f 6*0 8 27 0 0 0 63 9*0 12 5*0 23 7*0 35 7*0 74 14*0 2f 0 0 2f
  //   14 2f 17*0 32 7*0 28 52 41 5*0 52 23*0 67 2f 0 0 2f 14 2f 0 23 65 0 0 21 0 2e 9*0 1 7*0 23 65 74 5*0
  //   1 7*0 1 82*0 33 7*0 7 0 0 3f 15*0 37 4*0 7 0 0 3f 0 35 7 11 0 3f 5*0 34 0 0 0 47 12*0 b4 6*0 3f 15*0
  //   33 7*0 3f 0 3f 0 0 0 11 9*0 3 16*0 b4 8*0 3f 23*0 3f 0 0 0 11 0 3f 0 3f 0 0 0 32 19 15*0 34 3f 0 3f
  //   5 0 0 3f 0 0 0 3f 4*0 13 6*0 3f 7*0 3f 13 0 0 3f 0 0 0 3f 7*0 61 18*0 b4 36 22 24 5*0 61 13*0 33 0 0
  //   0 3e 0 33 42 7 5*0 11 0 3f 7*0 47 15*0 31 0 24 0 16 0 38 0 43 0 2 11*0 3f 0 3e 5*0 28 0 43 5*0 2
  //   27*0 24 3f 3f 0 0 0 3f 13*0 3f 7*0 7 0 3f 5*0 3f 7*0 61 85*0 44 15*0 7 14*0 42 7 6*0 8 0 0 44 0 7 0
  //   7 0 4f 15*0 5 30*0 8 10*0 13 21*0 5 13*0 41 7*0 16 8*0 4 10*0 82 0 0 0 94 15*0 45 4 6*0 31 0 0 0 43
  //   6 6*0 91 7*0 49 4 0 0 31 0 0 0 31 7*0 91 21*0 76 15*0 4f 10*0 42 7*0 67 6*0 13 0 4f 23*0 43 22*0 58
  //   41 7*0 4e 25*0 46 34 34 5*0 21 0 0 0 41 0 0 0 94 0 0 0 3 8*0 67 14*0 3 80*0 55 0 33 55 82 c1 0 0 17
  //   0 0 c1 52 8*0 57 7*0 9 0 0 82 0 0 19 4*0 52 0 0 0 18 4*0 58 19 0 0 44 9*0 55 94 c1 0 82 0 0 0 c1
  //   23*0 82 17*0 1 14*0 94 0 0 94 55 0 0 0 55 0 0 55 6 10*0 52 0 0 0 17 4*0 55 0 0 0 19 0 0 55 63 0 0 19
  //   0 0 0 54 69 0 0 91 11*0 19 23*0 33 39*0 55 82 c1 0 36 0 0 0 c1 52 0 0 0 18 8*0 44 0 52 0 0 0 17 0 0
  //   0 33 8*0 63 8*0 1 13*0 18 23*0 33 8*0 5f 6*0 5f 23*0 17 55 0 0 0 6 0 0 0 63 0 0 6 11*0 33 8*0 63 6*0
  //   63 7*0 91 161*0 63 7*0 36 23*0 4 14*0 67 0 0 67 55 0 0 67 55 0 0 55 4*0 29 0 0 41 64 0 0 76 7*0 67
  //   55 0 0 29 64 0 0 55 6f 6*0 54 64 0 0 64 6e 10*0 69 34 0 0 45 0 0 0 1 7*0 43 15*0 1 15*0 6f 21*0 66
  //   5*0 61 0 27 0 0 0 63 7*0 36 14*0 6f 8*0 4 19*0 24 5*0 18 5*0 4 29*0 6f 15*0 67 55 0 0 76 0 24 0 23
  //   6f 0 0 27 0 0 0 41 15*0 23 6f 6*0 6f 7*0 6f 112*0 74 74 b5 12*0 74 9 58 25*0 71 20*0 b5 b5 5*0 71 0
  //   0 0 8 0 0 0 11 39*0 76 9 0 0 11 4*0 b5 b5 0 79 2 21 0 72 0 0 0 39 0 0 0 32 16*0 74 0 26 0 26 6*0 39
  //   20*0 2 0 0 21 0 0 0 83 29*0 76 15*0 7 10*0 b5 87 13*0 11 0 7f 19*0 25 5*0 8 27*0 83 27*0 76 5 25 5*0
  //   11 7*0 11 0 0 0 11 9*0 7f 5*0 83 89*0 81 0 0 82 44 0 81 0 c5 0 c5 8 0 0 81 0 28 0 a7 0 0 0 6 8*0 82
  //   a7 0 0 8 0 0 c5 57 6*0 44 17*0 c5 0 82 a4 0 0 b2 0 0 0 71 0 0 0 93 15*0 82 8 0 0 8 0 0 0 71 25*0 c5
  //   0 0 a4 0 0 93 7*0 b2 16*0 57 14*0 82 0 0 0 97 15*0 49 27*0 49 7*0 8f 7*0 63 16*0 82 c5 0 0 26 0 0 93
  //   57 6*0 93 16*0 43 87 5 14*0 71 14*0 8 0 0 8 27*0 8 7*0 8f 24*0 57 32*0 71 5*0 8f 7*0 63 144*0 94 0
  //   26 0 a2 10*0 93 0 68 5*0 a2 7*0 91 a2 15 5*0 a2 7*0 a2 16*0 94 0 b3 94 26 1 0 93 0 15 13*0 a2 7*0 91
  //   b3 15 0 79 0 0 0 a2 7*0 a2 0 0 0 9f 12*0 26 0 0 26 0 0 0 a2 7*0 a2 7*0 9f 7*0 a2 7*0 9f 7*0 9f 23*0
  //   93 0 15 5*0 93 0 68 5*0 a2 7*0 91 0 27 5*0 a2 7*0 a2 16*0 26 6*0 a2 7*0 a2 15*0 a2 32*0 26 0 0 26 0
  //   0 0 a2 7*0 a2 0 0 0 9f 11*0 a2 15*0 9f 99*0 a7 0 4 5*0 26 5*0 a7 0 0 0 4 0 0 0 d5 7*0 4 0 4 16*0 a2
  //   18*0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
  //   Reset Button
  //   Who Goes
  //   First Button
endmodule
